# Fritzing sketch common_anode_led_controller (saved by Fritzing 0.9.4)
breadboards: 1

parts:
  WeMos_D1_Mini1 = WeMos D1 Mini
  Q1 = TRANSISTOR_NPN [package=to-92-ammo]
  Q3 = TRANSISTOR_NPN [package=to-92-ammo]
  Q4 = TRANSISTOR_NPN [package=to-92-ammo]
  R2 = Resistor [tolerance=±5% resistance=1k package="2010 [SMD]"]
  R6 = Resistor [tolerance=±5% resistance=1k package="2010 [SMD]"]
  R7 = Resistor [tolerance=±5% resistance=1k package="2010 [SMD]"]
  U2 = V_REG_MC33269 [package=dpak]

nets:
  N1: WeMos_D1_Mini1.3V3, U2.OUT
  N2: WeMos_D1_Mini1.D5, R2.Pin_0
  N3: WeMos_D1_Mini1.D6, R6.Pin_0
  N4: WeMos_D1_Mini1.D7, R7.Pin_0
  N5: WeMos_D1_Mini1.G, Q1.E, Q3.E, Q4.E, U2.GND
  N6: Q1.B, R2.Pin_1
  N7: Q3.B, R6.Pin_1
  N8: Q4.B, R7.Pin_1
