# Fritzing sketch common_cathode_led_controller (saved by Fritzing 0.9.4)
breadboards: 1

parts:
  WeMos_D1_Mini1 = WeMos D1 Mini
  Q1 = TRANSISTOR_NPN [package=to-92-ammo]
  Q2 = TRANSISTOR_PNP [package=to-92]
  Q3 = TRANSISTOR_NPN [package=to-92-ammo]
  Q4 = TRANSISTOR_NPN [package=to-92-ammo]
  Q5 = TRANSISTOR_PNP [package=to-92]
  Q6 = TRANSISTOR_PNP [package=to-92]
  R2 = Resistor [tolerance=±5% resistance=1k package="2010 [SMD]"]
  U2 = V_REG_MC33269 [package=dpak]
  R8 = Resistor [tolerance=±5% resistance=1k package="2010 [SMD]"]
  R9 = Resistor [tolerance=±5% resistance=1k package="2010 [SMD]"]
  R10 = Resistor [tolerance=±5% resistance=1k package="2010 [SMD]"]
  R11 = Resistor [tolerance=±5% resistance=1k package="2010 [SMD]"]
  R12 = Resistor [tolerance=±5% resistance=1k package="2010 [SMD]"]

nets:
  N1: WeMos_D1_Mini1.3V3, U2.OUT
  N2: WeMos_D1_Mini1.D5, R2.Pin_0
  N3: WeMos_D1_Mini1.D6, R8.Pin_0
  N4: WeMos_D1_Mini1.D7, R9.Pin_0
  N5: WeMos_D1_Mini1.G, Q1.E, Q3.E, Q4.E, U2.GND
  N6: Q1.B, R2.Pin_1
  N7: Q1.C, R10.Pin_1
  N8: Q2.E, Q5.E, Q6.E, U2.IN
  N9: Q2.B, R10.Pin_0
  N10: Q3.B, R8.Pin_1
  N11: Q3.C, R11.Pin_1
  N12: Q4.B, R9.Pin_1
  N13: Q4.C, R12.Pin_1
  N14: Q5.B, R11.Pin_0
  N15: Q6.B, R12.Pin_0
