# Fritzing sketch underglow (saved by Fritzing 0.9.4)
breadboards: 2

parts:
  WeMos_D1_Mini1 = WeMos D1 Mini
  Q1 = TRANSISTOR_NPN [package=to-92-ammo]
  Q2 = TRANSISTOR_PNP [package=to-92]
  Q3 = TRANSISTOR_NPN [package=to-92-ammo]
  Q4 = TRANSISTOR_NPN [package=to-92-ammo]
  Q5 = TRANSISTOR_PNP [package=to-92]
  Q6 = TRANSISTOR_PNP [package=to-92]
  R1 = Resistor [tolerance=±5% resistance=220 package="2010 [SMD]"]
  R2 = Resistor [tolerance=±5% resistance=220 package="2010 [SMD]"]
  LED1 = RGB LED (com. cathode, rgb) [package="5 mm [THT]"]
  R4 = Resistor [tolerance=±5% resistance=220 package="2010 [SMD]"]
  R5 = Resistor [tolerance=±5% resistance=220 package="2010 [SMD]"]
  R6 = Resistor [tolerance=±5% resistance=220 package="2010 [SMD]"]
  R7 = Resistor [tolerance=±5% resistance=220 package="2010 [SMD]"]
  LED2 = RGB LED (com. cathode, rgb) [package="5 mm [THT]"]
  LED3 = RGB LED (com. cathode, rgb) [package="5 mm [THT]"]
  LED4 = RGB LED (com. cathode, rgb) [package="5 mm [THT]"]
  R8 = Resistor [tolerance=±5% resistance=220 package="2010 [SMD]"]
  R9 = Resistor [tolerance=±5% resistance=220 package="2010 [SMD]"]
  R10 = Resistor [tolerance=±5% resistance=220 package="2010 [SMD]"]
  R11 = Resistor [tolerance=±5% resistance=220 package="2010 [SMD]"]
  R12 = Resistor [tolerance=±5% resistance=220 package="2010 [SMD]"]
  R13 = Resistor [tolerance=±5% resistance=220 package="2010 [SMD]"]
  R14 = Resistor [tolerance=±5% resistance=220 package="2010 [SMD]"]
  R15 = Resistor [tolerance=±5% resistance=220 package="2010 [SMD]"]
  R16 = Resistor [tolerance=±5% resistance=220 package="2010 [SMD]"]
  R17 = Resistor [tolerance=±5% resistance=220 package="2010 [SMD]"]
  R18 = Resistor [tolerance=±5% resistance=220 package="2010 [SMD]"]
  R19 = Resistor [tolerance=±5% resistance=220 package="2010 [SMD]"]
  U2 = V_REG_MC33269 [package=dpak]

nets:
  N1: WeMos_D1_Mini1.3V3, U2.OUT
  N2: WeMos_D1_Mini1.D5, R2.Pin_0
  N3: WeMos_D1_Mini1.D6, R6.Pin_0
  N4: WeMos_D1_Mini1.D7, R7.Pin_0
  N5: WeMos_D1_Mini1.G, Q1.E, Q3.E, Q4.E, LED1.common_cathode, LED2.common_cathode, LED3.common_cathode, LED4.common_cathode, U2.GND
  N6: Q1.B, R2.Pin_1
  N7: Q1.C, R1.Pin_1
  N8: Q2.E, Q5.E, Q6.E, U2.IN
  N9: Q2.B, R1.Pin_0
  N10: Q2.C, Q5.C, Q6.C, R8.Pin_0, R9.Pin_0, R10.Pin_0, R11.Pin_0, R12.Pin_0, R13.Pin_0, R14.Pin_0, R15.Pin_0, R16.Pin_0, R17.Pin_0, R18.Pin_0, R19.Pin_0
  N11: Q3.B, R6.Pin_1
  N12: Q3.C, R4.Pin_1
  N13: Q4.B, R7.Pin_1
  N14: Q4.C, R5.Pin_1
  N15: Q5.B, R4.Pin_0
  N16: Q6.B, R5.Pin_0
  N17: LED1.red_anode, R10.Pin_1
  N18: LED1.green_anode, R9.Pin_1
  N19: LED1.blue_anode, R8.Pin_1
  N20: LED2.red_anode, R19.Pin_1
  N21: LED2.green_anode, R18.Pin_1
  N22: LED2.blue_anode, R14.Pin_1
  N23: LED3.red_anode, R13.Pin_1
  N24: LED3.green_anode, R12.Pin_1
  N25: LED3.blue_anode, R11.Pin_1
  N26: LED4.red_anode, R17.Pin_1
  N27: LED4.green_anode, R16.Pin_1
  N28: LED4.blue_anode, R15.Pin_1
